// Logisim project lookoverhead.circ as structural Verilog: 1 circuit, main circuit main
module main (
  input  in_1,
  input  in_2,
  input  [3:0] in_3,
  input  [3:0] in_4,
  input  in_5,
  input  in_6,
  input  in_7,
  input  in_8,
  input  in_9,
  input  in_10,
  input  in_11,
  output out_12,
  output [3:0] out_13
);

  wire and_1_out, and_2_out, and_3_out, and_4_out, and_5_out, and_6_out, and_7_out, and_8_out, and_9_out,
       and_10_out, and_11_out, and_12_out, and_13_out, and_14_out, and_15_out, and_16_out, or_1_out,
       or_2_out, or_3_out, or_4_out, xor_1_out, xor_2_out, xor_3_out, xor_4_out;

  xor xor_1 (xor_1_out, in_1, in_2);
  and and_1 (and_1_out, in_1, in_2);
  xor xor_2 (xor_2_out, in_5, in_6);
  and and_2 (and_2_out, in_5, in_6);
  xor xor_3 (xor_3_out, in_7, in_8);
  and and_3 (and_3_out, in_7, in_8);
  xor xor_4 (xor_4_out, in_9, in_10);
  and and_4 (and_4_out, in_9, in_10);
  and and_5 (and_5_out, xor_1_out, and_11_out);
  and and_6 (and_6_out, xor_1_out, and_9_out);
  and and_7 (and_7_out, and_2_out, xor_1_out);
  and and_8 (and_8_out, xor_3_out, and_4_out, xor_2_out);
  and and_9 (and_9_out, xor_2_out, and_12_out);
  and and_10 (and_10_out, xor_3_out, and_4_out, xor_2_out);
  and and_11 (and_11_out, xor_2_out, and_3_out);
  and and_12 (and_12_out, in_11, xor_4_out, xor_3_out);
  and and_13 (and_13_out, in_11, xor_4_out, xor_3_out);
  and and_14 (and_14_out, xor_3_out, and_4_out);
  and and_15 (and_15_out, in_11, xor_4_out);
  or or_1 (or_1_out, and_7_out, and_6_out, and_16_out, and_5_out, and_1_out);
  and and_16 (and_16_out, xor_1_out, and_8_out);
  or or_2 (or_2_out, and_10_out, and_9_out, and_11_out, and_2_out);
  or or_3 (or_3_out, and_13_out, and_14_out, and_3_out);
  or or_4 (or_4_out, and_15_out, and_4_out);
  xor xor_5 (out_12, or_1_out, xor_1_out);
  xor xor_6 (out_13[3], or_2_out, xor_2_out);
  xor xor_7 (out_13[2], or_3_out, xor_3_out);
  xor xor_8 (out_13[1], or_4_out, xor_4_out);
  xor xor_9 (out_13[0], in_11, xor_4_out);

  // Notes on the sheet:
  //   c4
  //   s3
  //   s1
  //   s0
  //   s2
endmodule
